// Logisim project CPU.circ as structural Verilog: 1 circuit, main circuit main
module main (
  output [15:0] Zero,
  output [15:0] Zero_2,
  output [15:0] Zero_3,
  output [15:0] Zero_4,
  output [15:0] out_5,
  output Zero_5,
  output [2:0] Zero_6,
  output [2:0] Zero_7,
  output [15:0] out_9,
  output [5:0] Zero_8,
  output [3:0] Zero_9,
  output [15:0] Zero_10,
  output [2:0] out_13
);

  wire Beq_out, CLK_out, main_2_alu_src, main_2_branch, main_2_jump, main_2_mem_read, main_2_mem_write,
       main_2_memtoreg, main_2_regdst, main_2_regwrite, Reset_out;
  wire [1:0] main_2_aluop;
  wire [2:0] multiplexer_1_out;
  wire [15:0] adder_1_out, adder_2_out, multiplexer_2_out, multiplexer_3_out, multiplexer_4_out, PC_q,
       ram_1_data;

  Register #(.width(16)) PC (.D(multiplexer_4_out), .Q(PC_q), .clk(CLK_out), .clr(Reset_out));  // open: en
  Clock CLK (.out(CLK_out));
  Button Reset (.out(Reset_out));
  Adder #(.width(16)) adder_1 (.a(PC_q), .b(16'h1), .out(adder_1_out));  // open: cin, cout
  ROM #(.addrWidth(16), .dataWidth(16)) rom_1 (.addr(PC_q), .data({Zero_9, Zero_6, Zero_7, Zero_8}));  // open: sel
  Jump_main main_1 (.PC(adder_1_out), .Instruction({Zero_9, Zero_6, Zero_7, Zero_8}), .jump(Zero));
  Control_unit_main main_2 (
    .in_1(Zero_9), .RegDst(main_2_regdst), .RegWrite(main_2_regwrite), .ALU_SRC(main_2_alu_src),
    .Mem_Read(main_2_mem_read), .Mem_Write(main_2_mem_write), .MemToReg(main_2_memtoreg),
    .Branch(main_2_branch), .AlUOp(main_2_aluop), .Jump(main_2_jump));
  Multiplexer #(.width(3)) multiplexer_1 (
    .in0(Zero_7), .in1(Zero_8[5:3]), .out(multiplexer_1_out), .sel(main_2_regdst));  // open: en
  assign Zero_10 = {{10{Zero_8[5]}}, Zero_8};  // Bit_Extender bit_extender_1
  Register_file_main main_3 (
    .WriteData(out_9), .Write_Register(multiplexer_1_out), .RegWrite(main_2_regwrite), .Read_data_1(Zero_3),
    .Read_register_1__rs(Zero_6), .Read_data_2(out_5), .Read_register_2__rt(Zero_7), .clk(CLK_out));
  Adder #(.width(16)) adder_2 (.a(adder_1_out), .b(Zero_10), .out(adder_2_out));  // open: cin, cout
  Multiplexer #(.width(16)) multiplexer_2 (
    .in0(out_5), .in1(Zero_10), .out(multiplexer_2_out), .sel(main_2_alu_src));  // open: en
  ALU_Control_Unit_main main_4 (.out_3(out_13), .ALUOp(main_2_aluop), .Funct(Zero_8[2:0]));
  Multiplexer #(.width(16)) multiplexer_3 (
    .in0(adder_1_out), .in1(adder_2_out), .out(multiplexer_3_out), .sel(Beq_out));  // open: en
  and Beq (Beq_out, main_2_branch, Zero_5);
  _16_bit_alu u_16_bit_alu_1 (
    .B(multiplexer_2_out), .A(Zero_3), .ALU_Op(out_13[1:0]), .result(Zero_2), .zero(Zero_5),
    .B_Inv(out_13[2]), .Cin(out_13[2]));  // open: Overflow
  Multiplexer #(.width(16)) multiplexer_4 (
    .in0(multiplexer_3_out), .in1(Zero), .out(multiplexer_4_out), .sel(main_2_jump));  // open: en
  RAM #(.addrWidth(16), .dataWidth(16), .bus("separate")) ram_1 (
    .addr(Zero_2), .din(out_5), .data(ram_1_data), .str(main_2_mem_write), .clk(CLK_out), .ld(main_2_mem_read));  // open: sel, clr
  Multiplexer #(.width(16)) multiplexer_5 (
    .in0(Zero_2), .in1(ram_1_data), .out(out_9), .sel(main_2_memtoreg));  // open: en

  assign Zero_4 = out_5;

  // Notes on the sheet:
  //   contents of rom_1 (hex, n*v repeats v):
  //   9040 9081 90c2 4e0 728 9103 b31 a184 9184 d008
  //   I-Format
endmodule
